# Fritzing sketch XL4016X2 (saved by Fritzing 0.9.3b)
circuit board: 8.46667cm x 5.64444cm
perfboards: 3

parts:
  J1_SOLAR_PANEL = Screw terminal - 2 pins [package=THT]
  D2 = TVS Diode 47V [part_number=P6KE47CA]
  R1 = Resistor [tolerance=±5% resistance=100k package=THT]
  R2 = Resistor [tolerance=±5% resistance=15k package=THT]
  C1 = Ceramic Capacitor [capacitance=100nF package="100 mil [THT, multilayer]"]
  Part1 = ACS712 Low Current Sensor Board v12
  C1_1_LOW_ESR = Electrolytic Capacitor [capacitance=100µF voltage=50V package="100 mil [THT, electrolytic]"]
  C1_3 = Electrolytic Capacitor [capacitance=100µF voltage=50V package="100 mil [THT, electrolytic]"]
  C1_2 = Electrolytic Capacitor [capacitance=100µF voltage=50V package="100 mil [THT, electrolytic]"]
  C1_4 = Electrolytic Capacitor [capacitance=100µF voltage=50V package="100 mil [THT, electrolytic]"]
  J7_BATTERY = Screw terminal - 2 pins [package=THT]
  R3 = Resistor [tolerance=±5% resistance=100k package=THT]
  R4 = Resistor [tolerance=±5% resistance=47k package=THT]
  Part2 = ACS712 Low Current Sensor Board v12
  C6 = Ceramic Capacitor [capacitance=100nF package="100 mil [THT, multilayer]"]
  Fuse1 = Fuse with Handler [part_number=Htc-15m]
  U1 = MP2307Module [part_number=MP2307 package=THT]
  J2_BUCK1_IN = Screw terminal - 2 pins [package=THT]
  J5_BUCK2_IN = Screw terminal - 2 pins [package=THT]
  J4_BUCK1_OUT = Screw terminal - 2 pins [package=THT]
  J6_BUCK2_OUT = Screw terminal - 2 pins [package=THT]
  J3_LOAD = Screw terminal - 2 pins [package=THT]
  Q2_IRF4905 = Basic FET P-Channel [package="TO220 [THT]"]
  R2_2 = Resistor [tolerance=±5% resistance=100k package=THT]
  Q5 = NPN-Transistor [package="TO92 [THT]"]  # not connected
  R4_2 = Resistor [tolerance=±5% resistance=10k package=THT]  # not connected
  D1 = Diode [package=diode-1n4148]
  D2_2 = Diode [package=diode-1n4148]
  Q4 = PNP-Transistor [package="TO92 [THT]"]
  R7 = Resistor [tolerance=±5% resistance=47k package=THT]
  Q3 = PNP-Transistor [package="TO92 [THT]"]
  R6 = Resistor [tolerance=±5% resistance=22k package=THT]  # not connected
  Q3_IRF4905 = Basic FET P-Channel [package="TO220 [THT]"]
  D5 = Diode [package=diode-1n4148]
  D6 = Diode [package=diode-1n4148]
  Q7 = PNP-Transistor [package="TO92 [THT]"]
  R10 = Resistor [tolerance=±5% resistance=47k package=THT]
  Q8 = PNP-Transistor [package="TO92 [THT]"]
  R9 = Resistor [tolerance=±5% resistance=22k package=THT]
  Q1_IRF4905 = Basic FET P-Channel [package="TO220 [THT]"]

nets:
  N1: J1_SOLAR_PANEL.pin1, D2.anode
  N2: J1_SOLAR_PANEL.pin2, D2.cathode
  N3: R1.Pin_0, R2.Pin_1, C1.0
  GND: R2.Pin_0, C1.1, Part1.GND, C1_1_LOW_ESR.-, C1_3.-, C1_2.-, C1_4.-, J7_BATTERY.pin1, R4.Pin_0, Part2.GND, C6.1, U1.IN-, U1.OUT-, J2_BUCK1_IN.pin2, J5_BUCK2_IN.pin2, J4_BUCK1_OUT.pin2, J6_BUCK2_OUT.pin2, J3_LOAD.pin2, R7.Pin_1, R10.Pin_1, R9.Pin_1
  N4: Part1.IP+, C1_1_LOW_ESR.+, C1_3.+, C1_2.+, C1_4.+, J2_BUCK1_IN.pin1, J5_BUCK2_IN.pin1
  5V: Part1.5V, Part2.5V, U1.OUT+
  N5: J7_BATTERY.pin2, Fuse1.Connector1
  N6: R3.Pin_0, R4.Pin_1, C6.0
  N7: R3.Pin_1, Fuse1.Connector2, U1.IN+
  N8: J4_BUCK1_OUT.pin1, Q1_IRF4905.drain
  N9: J6_BUCK2_OUT.pin1, Q3_IRF4905.drain
  N10: J3_LOAD.pin1, Q2_IRF4905.drain
  N11: Q2_IRF4905.gate, R2_2.Pin_1
  N12: Q2_IRF4905.source, R2_2.Pin_0, Q3_IRF4905.source, Q1_IRF4905.source
  N13: D1.C, Q3.E
  N14: D2_2.C, Q4.E
  N15: Q4.B, Q3.B, Q3.C
  N16: Q4.C, R7.Pin_0
  N17: Q3_IRF4905.gate, Q7.C, R10.Pin_0
  N18: D5.C, Q8.E
  N19: D6.C, Q7.E
  N20: Q7.B, Q8.B, Q8.C, R9.Pin_0

custom parts:
  TVS Diode 47V: A transient voltage suppressor diode
  MP2307Module: DC-DC converter based on MP2307 IC
